// Digital circuit SERV_alu_1.dig as structural Verilog
module SERV_alu_1 (
  input  i_rs1,
  input  i_opb,
  input  i_en,
  input  clk,
  input  i_boolop0,
  input  i_cmpsig,
  input  i_sub,
  input  i_cmpeq,
  input  i_cnt0,
  input  i_rdsel0,
  input  i_buf,
  input  i_rdsel1,
  input  i_rdsel2,
  input  i_boolop1,
  output o_cmp,
  output o_rd
);

  wire add_1_s, add_2_c_o, add_2_s, and_1_out, and_2_out, and_3_out, and_4_out, and_5_out, and_6_out,
       and_7_out, and_8_out, and_9_out, d_ff_1_q, d_ff_2_q, multiplexer_1_out, multiplexer_3_out, not_1_out,
       not_2_out, not_3_out, or_1_out, or_2_out, xor_1_out, xor_2_out;

  xor xor_1 (xor_1_out, i_rs1, i_opb);
  and and_1 (and_1_out, i_rs1, i_cmpsig);
  and and_2 (and_2_out, i_cmpsig, i_opb);
  xor xor_2 (xor_2_out, i_opb, i_sub);
  Multiplexer multiplexer_1 (.sel(i_en), .in_0(i_sub), .in_1(add_2_c_o), .out(multiplexer_1_out));
  not not_1 (not_1_out, i_boolop0);
  D_FF d_ff_1 (.D(multiplexer_1_out), .C(clk), .Q(d_ff_1_q));  // open: nQ
  and and_3 (and_3_out, xor_1_out, not_1_out);
  and and_4 (and_4_out, i_boolop1, i_rs1, i_opb);
  not not_2 (not_2_out, and_2_out);
  or or_1 (or_1_out, and_3_out, and_4_out);
  Add add_1 (.a(and_1_out), .b(not_2_out), .c_i(add_2_c_o), .s(add_1_s));  // open: c_o
  Add add_2 (.a(i_rs1), .b(xor_2_out), .c_i(d_ff_1_q), .s(add_2_s), .c_o(add_2_c_o));
  not not_3 (not_3_out, add_2_s);
  or or_2 (or_2_out, i_cnt0, d_ff_2_q);
  and and_5 (and_5_out, d_ff_2_q, i_cnt0);
  and and_6 (and_6_out, i_rdsel2, or_1_out);
  and and_7 (and_7_out, i_rdsel0, add_2_s);
  and and_8 (and_8_out, i_rdsel1, and_5_out);
  and and_9 (and_9_out, not_3_out, or_2_out);
  D_FF d_ff_2 (.D(multiplexer_3_out), .C(clk), .Q(d_ff_2_q));  // open: nQ
  or or_3 (o_rd, i_buf, and_6_out, and_7_out, and_8_out);
  Multiplexer multiplexer_2 (.sel(i_cmpeq), .in_0(add_1_s), .in_1(and_9_out), .out(o_cmp));
  Multiplexer multiplexer_3 (.sel(i_en), .in_0(d_ff_2_q), .in_1(o_cmp), .out(multiplexer_3_out));

  // Notes on the sheet:
  //   SERV ALU
  //   Bool Expressions
  //   Add/Subtract
  //   Comparator
  //   Output Selector
endmodule
